# Fritzing sketch RFID (saved by Fritzing 0.8.7b)

parts:
  Onderdeel1 = Arduino Uno (Rev3)
  U1 = RFID RC522 SIP - 8 pins [chip_label="RFID RC522" package="SIP (Single Inline) [THT]"]

nets:
  N1: Onderdeel1.D10_PWM/SS, U1.IRQ
  N2: Onderdeel1.D11_PWM/MOSI, U1.SCK
  N3: Onderdeel1.D12/MISO, U1.MOSI
  N4: Onderdeel1.D13/SCK, U1.NSS
  3V3: Onderdeel1.3V3, U1.VCC
  GND: Onderdeel1.GND, U1.GND

custom parts:
  RFID RC522 SIP - 8 pins: A SIP stand-in part for RFID RC522 . With 8 pins on a 300 mil single inline package (SIP) footprint.
