# Fritzing sketch Alles (saved by Fritzing 0.8.7b)
breadboards: 1

parts:
  Onderdeel1 = Arduino Mega ADK (Rev3)
  MOTOR1 = 28BYJ-48 Stepper Motor
  BREAKOUT2 = ULN2003A breakout board
  MOTOR2 = 28BYJ-48 Stepper Motor
  BREAKOUT3 = ULN2003A breakout board
  MOTOR3 = 28BYJ-48 Stepper Motor
  BREAKOUT1 = ULN2003A breakout board
  Onderdeel2 = RFID-RC522 [part_number=101218]
  Keypad4x1 = Keypad Membran 4x4
  Onderdeel3 = Thermal Printer
  S1 = Pushbutton [package="[THT]"]
  S2 = Pushbutton [package="[THT]"]
  S3 = Pushbutton [package="[THT]"]
  S4 = Pushbutton [package="[THT]"]
  S5 = Pushbutton [package="[THT]"]
  S6 = Pushbutton [package="[THT]"]
  S7 = Pushbutton [package="[THT]"]
  S8 = Pushbutton [package="[THT]"]

nets:
  GND: Onderdeel1.GND, BREAKOUT2.0V, BREAKOUT3.0V, BREAKOUT1.0V, Onderdeel2.GND, Onderdeel3.GND#2
  N1: Onderdeel1.D13_PWM, S1.Pin_3, S1.Pin_4
  N2: Onderdeel1.D12_PWM, S2.Pin_3, S2.Pin_4
  N3: Onderdeel1.D11_PWM, S3.Pin_3, S3.Pin_4
  N4: Onderdeel1.D10_PWM, S4.Pin_3, S4.Pin_4
  N5: Onderdeel1.D9_PWM, S5.Pin_3, S5.Pin_4
  N6: Onderdeel1.D8_PWM, S6.Pin_3, S6.Pin_4
  3V3: Onderdeel1.3V3, Onderdeel2.3.3V
  +5V: Onderdeel1.5V, BREAKOUT2.+5V, BREAKOUT3.+5V, BREAKOUT1.+5V
  N7: Onderdeel1.VIN, S1.Pin_1, S1.Pin_2, S3.Pin_1, S3.Pin_2, S5.Pin_1, S5.Pin_2, S7.Pin_1, S7.Pin_2, S8.Pin_1, S8.Pin_2
  N8: Onderdeel1.D6_PWM, S8.Pin_3, S8.Pin_4
  N9: Onderdeel1.D7_PWM, S7.Pin_3, S7.Pin_4
  N10: Onderdeel1.D23, BREAKOUT3.In_1
  N11: Onderdeel1.D25, BREAKOUT3.In_2
  N12: Onderdeel1.D26, BREAKOUT1.In_1
  N13: Onderdeel1.D27, BREAKOUT3.In_3
  N14: Onderdeel1.D28, BREAKOUT1.In_2
  N15: Onderdeel1.D29, BREAKOUT3.In_4
  N16: Onderdeel1.D30, BREAKOUT1.In_3
  N17: Onderdeel1.D32, BREAKOUT1.In_4
  N18: Onderdeel1.D34, BREAKOUT2.In_1
  N19: Onderdeel1.D36, BREAKOUT2.In_2
  N20: Onderdeel1.D37, Onderdeel3.TXD
  N21: Onderdeel1.D38, BREAKOUT2.In_3
  N22: Onderdeel1.D39, Onderdeel3.RXD
  N23: Onderdeel1.D40, BREAKOUT2.In_4
  N24: Onderdeel1.D42, Keypad4x1.Pin1
  N25: Onderdeel1.D43, Keypad4x1.Pin5
  N26: Onderdeel1.D44, Keypad4x1.Pin2
  N27: Onderdeel1.D45, Keypad4x1.Pin6
  N28: Onderdeel1.D46, Keypad4x1.Pin3
  N29: Onderdeel1.D47, Keypad4x1.Pin7
  N30: Onderdeel1.D48, Keypad4x1.Pin4
  N31: Onderdeel1.D49, Keypad4x1.Pin8
  N32: Onderdeel1.D50/MISO, Onderdeel2.MISO
  N33: Onderdeel1.D51/MOSI, Onderdeel2.MOSI
  N34: Onderdeel1.D52/SCK, Onderdeel2.SCK
  N35: Onderdeel1.D53/SS, Onderdeel2.SDA
  N36: MOTOR1.BLUE, BREAKOUT1.PINK_wire
  N37: MOTOR1.PINK, BREAKOUT1.BLUE_wire
  N38: MOTOR1.RED, BREAKOUT1.RED_wire
  N39: MOTOR1.ORANGE, BREAKOUT1.YELLOW_wire
  N40: MOTOR1.YELLOW, BREAKOUT1.ORANGE_wire
  N41: BREAKOUT2.RED_wire, MOTOR2.RED
  N42: BREAKOUT2.ORANGE_wire, MOTOR2.YELLOW
  N43: BREAKOUT2.YELLOW_wire, MOTOR2.ORANGE
  N44: BREAKOUT2.PINK_wire, MOTOR2.BLUE
  N45: BREAKOUT2.BLUE_wire, MOTOR2.PINK
  N46: BREAKOUT3.RED_wire, MOTOR3.RED
  N47: BREAKOUT3.ORANGE_wire, MOTOR3.YELLOW
  N48: BREAKOUT3.YELLOW_wire, MOTOR3.ORANGE
  N49: BREAKOUT3.PINK_wire, MOTOR3.BLUE
  N50: BREAKOUT3.BLUE_wire, MOTOR3.PINK
  N51: S2.Pin_1, S2.Pin_2
  N52: S4.Pin_1, S4.Pin_2
  N53: S6.Pin_1, S6.Pin_2

custom parts:
  28BYJ-48 Stepper Motor: 28BYJ-48 gear-reduction stepper motor (small)
  ULN2003A breakout board: ULN2003A 7-way Darlington Transistor Driver on breakoutboard
  Keypad Membran 4x4: Membrane Keypad 4x4 Matrix
