# Fritzing sketch Keypad (saved by Fritzing 0.8.7b)

parts:
  Onderdeel1 = Arduino Uno (Rev3)
  Keypad4x2 = Keypad Membran 4x4

nets:
  N1: Onderdeel1.D8, Keypad4x2.Pin2
  N2: Onderdeel1.D9_PWM, Keypad4x2.Pin1
  N3: Onderdeel1.D2, Keypad4x2.Pin8
  N4: Onderdeel1.D3_PWM, Keypad4x2.Pin7
  N5: Onderdeel1.D4, Keypad4x2.Pin6
  N6: Onderdeel1.D5_PWM, Keypad4x2.Pin5
  N7: Onderdeel1.D6_PWM, Keypad4x2.Pin4
  N8: Onderdeel1.D7, Keypad4x2.Pin3

custom parts:
  Keypad Membran 4x4: Membrane Keypad 4x4 Matrix
