# Fritzing sketch KeypadenRFID (saved by Fritzing 0.8.7b)

parts:
  Onderdeel1 = Arduino Uno (Rev3)
  U1 = RFID RC522 SIP - 8 pins [chip_label="RFID RC522" package="SIP (Single Inline) [THT]"]
  Keypad4x1 = Keypad Membran 4x4

nets:
  N1: Onderdeel1.D8, Keypad4x1.Pin2
  N2: Onderdeel1.D9_PWM, Keypad4x1.Pin1
  N3: Onderdeel1.D10_PWM/SS, U1.IRQ
  N4: Onderdeel1.D11_PWM/MOSI, U1.SCK
  N5: Onderdeel1.D12/MISO, U1.MOSI
  N6: Onderdeel1.D13/SCK, U1.NSS
  N7: Onderdeel1.D2, Keypad4x1.Pin8
  N8: Onderdeel1.D3_PWM, Keypad4x1.Pin7
  N9: Onderdeel1.D4, Keypad4x1.Pin6
  N10: Onderdeel1.D5_PWM, Keypad4x1.Pin5
  N11: Onderdeel1.D6_PWM, Keypad4x1.Pin4
  N12: Onderdeel1.D7, Keypad4x1.Pin3
  3V3: Onderdeel1.3V3, U1.VCC
  GND: Onderdeel1.GND, U1.GND

custom parts:
  RFID RC522 SIP - 8 pins: A SIP stand-in part for RFID RC522 . With 8 pins on a 300 mil single inline package (SIP) footprint.
  Keypad Membran 4x4: Membrane Keypad 4x4 Matrix
