# Fritzing sketch Motor (saved by Fritzing 0.8.7b)

parts:
  BREAKOUT1 = ULN2003A breakout board
  MOTOR1 = 28BYJ-48 Stepper Motor
  Onderdeel1 = Arduino Uno (Rev3) - ICSP

nets:
  N1: BREAKOUT1.In_1, Onderdeel1.D5_PWM
  N2: BREAKOUT1.In_2, Onderdeel1.D4
  N3: BREAKOUT1.In_3, Onderdeel1.D3_PWM
  N4: BREAKOUT1.In_4, Onderdeel1.D2
  N5: BREAKOUT1.0V, Onderdeel1.GND
  +5V: BREAKOUT1.+5V, Onderdeel1.5V
  N6: BREAKOUT1.RED_wire, MOTOR1.RED
  N7: BREAKOUT1.ORANGE_wire, MOTOR1.YELLOW
  N8: BREAKOUT1.YELLOW_wire, MOTOR1.ORANGE
  N9: BREAKOUT1.PINK_wire, MOTOR1.BLUE
  N10: BREAKOUT1.BLUE_wire, MOTOR1.PINK

custom parts:
  ULN2003A breakout board: ULN2003A 7-way Darlington Transistor Driver on breakoutboard
  28BYJ-48 Stepper Motor: 28BYJ-48 gear-reduction stepper motor (small)
